// Logisim project ALU_FINAL.circ as structural Verilog: 1 circuit, main circuit main
module main (
  input  in_1,
  input  in_2,
  input  in_3,
  input  in_4,
  input  in_5,
  input  in_6,
  input  in_7,
  input  in_8,
  input  in_9,
  input  in_10,
  input  in_11,
  input  in_12,
  input  in_13,
  input  in_14,
  input  in_15,
  input  in_16,
  input  in_17,
  input  in_18,
  input  in_19,
  input  in_20,
  input  in_21,
  input  in_22,
  input  in_23,
  input  in_24,
  input  in_25,
  input  in_26,
  input  in_27,
  input  in_28,
  input  in_29,
  input  in_30,
  input  in_31,
  input  in_32,
  input  A15,
  input  in_34,
  input  [1:0] S2,
  input  in_36
);

  wire adder_1_cout, adder_1_out, adder_2_cout, adder_2_out, adder_3_cout, adder_3_out, adder_4_cout,
       adder_4_out, adder_5_cout, adder_5_out, adder_6_cout, adder_6_out, adder_7_cout, adder_7_out,
       adder_8_cout, adder_8_out, adder_9_cout, adder_9_out, adder_10_cout, adder_10_out, adder_11_cout,
       adder_11_out, adder_12_cout, adder_12_out, adder_13_cout, adder_13_out, adder_14_cout, adder_14_out,
       adder_15_cout, adder_15_out, adder_16_cout, adder_16_out, and_1_out, and_2_out, and_3_out, and_4_out,
       and_5_out, and_6_out, and_7_out, and_8_out, and_9_out, and_10_out, and_11_out, and_12_out, and_13_out,
       and_14_out, and_15_out, and_16_out, multiplexer_1_out, multiplexer_2_out, multiplexer_3_out,
       multiplexer_4_out, multiplexer_5_out, multiplexer_6_out, multiplexer_7_out, multiplexer_8_out,
       multiplexer_9_out, multiplexer_10_out, multiplexer_11_out, multiplexer_12_out, multiplexer_13_out,
       multiplexer_14_out, multiplexer_15_out, multiplexer_16_out, multiplexer_17_out, multiplexer_18_out,
       multiplexer_19_out, multiplexer_20_out, multiplexer_21_out, multiplexer_22_out, multiplexer_23_out,
       multiplexer_24_out, multiplexer_25_out, multiplexer_26_out, multiplexer_27_out, multiplexer_28_out,
       multiplexer_29_out, multiplexer_30_out, multiplexer_31_out, multiplexer_32_out, not_1_out, not_2_out,
       not_3_out, not_4_out, not_5_out, not_6_out, not_7_out, not_8_out, not_9_out, not_10_out, not_11_out,
       not_12_out, not_13_out, not_14_out, not_15_out, not_16_out, or_1_out, or_2_out, or_3_out, or_4_out,
       or_5_out, or_6_out, or_7_out, or_8_out, or_9_out, or_10_out, or_11_out, or_12_out, or_13_out,
       or_14_out, or_15_out, or_16_out, undriven, xor_1_out, xor_2_out, xor_3_out, xor_4_out, xor_5_out,
       xor_6_out, xor_7_out, xor_8_out, xor_9_out, xor_10_out, xor_11_out, xor_12_out, xor_13_out,
       xor_14_out, xor_15_out, xor_16_out, xor_17_out, xor_18_out, xor_19_out, xor_20_out, xor_21_out,
       xor_22_out, xor_23_out, xor_24_out, xor_25_out, xor_26_out, xor_27_out, xor_28_out, xor_29_out,
       xor_30_out, xor_31_out, xor_32_out;

  xor xor_1 (xor_1_out, in_1, in_17);
  xor xor_2 (xor_2_out, in_2, in_17);
  xor xor_3 (xor_3_out, in_3, in_17);
  xor xor_4 (xor_4_out, in_4, in_17);
  xor xor_5 (xor_5_out, in_5, in_17);
  xor xor_6 (xor_6_out, in_6, in_17);
  xor xor_7 (xor_7_out, in_7, in_17);
  xor xor_8 (xor_8_out, in_8, in_17);
  and and_1 (and_1_out, in_19, in_1);
  or or_1 (or_1_out, in_19, in_1);
  xor xor_9 (xor_9_out, in_19, in_1);
  not not_1 (not_1_out, in_19);
  and and_2 (and_2_out, in_20, in_2);
  or or_2 (or_2_out, in_20, in_2);
  xor xor_10 (xor_10_out, in_20, in_2);
  not not_2 (not_2_out, in_20);
  and and_3 (and_3_out, in_21, in_3);
  or or_3 (or_3_out, in_21, in_3);
  xor xor_11 (xor_11_out, in_21, in_3);
  not not_3 (not_3_out, in_21);
  and and_4 (and_4_out, in_22, in_4);
  or or_4 (or_4_out, in_22, in_4);
  xor xor_12 (xor_12_out, in_22, in_4);
  not not_4 (not_4_out, in_22);
  not not_5 (not_5_out, in_23);
  not not_6 (not_6_out, in_24);
  not not_7 (not_7_out, in_25);
  not not_8 (not_8_out, in_26);
  Adder #(.width(1)) adder_1 (.a(in_19), .b(xor_1_out), .out(adder_1_out), .cin(in_18), .cout(adder_1_cout));
  Adder #(.width(1)) adder_2 (.a(in_20), .b(xor_2_out), .out(adder_2_out), .cin(adder_1_cout), .cout(adder_2_cout));
  Adder #(.width(1)) adder_3 (.a(in_21), .b(xor_3_out), .out(adder_3_out), .cin(adder_2_cout), .cout(adder_3_cout));
  Adder #(.width(1)) adder_4 (.a(in_22), .b(xor_4_out), .out(adder_4_out), .cin(adder_3_cout), .cout(adder_4_cout));
  Adder #(.width(1)) adder_5 (.a(in_23), .b(xor_5_out), .out(adder_5_out), .cin(adder_4_cout), .cout(adder_5_cout));
  Adder #(.width(1)) adder_6 (.a(in_24), .b(xor_6_out), .out(adder_6_out), .cin(adder_5_cout), .cout(adder_6_cout));
  Adder #(.width(1)) adder_7 (.a(in_25), .b(xor_7_out), .out(adder_7_out), .cin(adder_6_cout), .cout(adder_7_cout));
  Adder #(.width(1)) adder_8 (.a(in_26), .b(xor_8_out), .out(adder_8_out), .cin(adder_7_cout), .cout(adder_8_cout));
  Multiplexer #(.select(2)) multiplexer_1 (
    .in0(and_1_out), .in1(or_1_out), .in2(xor_9_out), .in3(not_1_out), .out(multiplexer_1_out), .sel(S2));
  Multiplexer #(.select(2)) multiplexer_2 (
    .in0(and_2_out), .in1(or_2_out), .in2(xor_10_out), .in3(not_2_out), .out(multiplexer_2_out), .sel(S2));
  Multiplexer #(.select(2)) multiplexer_3 (
    .in0(and_3_out), .in1(or_3_out), .in2(xor_11_out), .in3(not_3_out), .out(multiplexer_3_out), .sel(S2));
  Multiplexer #(.select(2)) multiplexer_4 (
    .in0(and_4_out), .in1(or_4_out), .in2(xor_12_out), .in3(not_4_out), .out(multiplexer_4_out), .sel(S2));
  and and_5 (and_5_out, in_23, in_5);
  or or_5 (or_5_out, in_23, in_5);
  Multiplexer #(.select(2)) multiplexer_5 (
    .in0(and_5_out), .in1(or_5_out), .in2(xor_13_out), .in3(not_5_out), .out(multiplexer_5_out), .sel(S2));
  xor xor_13 (xor_13_out, in_23, in_5);
  and and_6 (and_6_out, in_24, in_6);
  or or_6 (or_6_out, in_24, in_6);
  Multiplexer #(.select(2)) multiplexer_6 (
    .in0(and_6_out), .in1(or_6_out), .in2(xor_14_out), .in3(not_6_out), .out(multiplexer_6_out), .sel(S2));
  xor xor_14 (xor_14_out, in_24, in_6);
  and and_7 (and_7_out, in_25, in_7);
  or or_7 (or_7_out, in_25, in_7);
  Multiplexer #(.select(2)) multiplexer_7 (
    .in0(and_7_out), .in1(or_7_out), .in2(xor_15_out), .in3(not_7_out), .out(multiplexer_7_out), .sel(S2));
  xor xor_15 (xor_15_out, in_25, in_7);
  and and_8 (and_8_out, in_26, in_8);
  or or_8 (or_8_out, in_26, in_8);
  Multiplexer #(.select(2)) multiplexer_8 (
    .in0(and_8_out), .in1(or_8_out), .in2(xor_16_out), .in3(not_8_out), .out(multiplexer_8_out), .sel(S2));
  xor xor_16 (xor_16_out, in_26, in_8);
  and and_9 (and_9_out, in_27, in_9);
  or or_9 (or_9_out, in_27, in_9);
  xor xor_17 (xor_17_out, in_27, in_9);
  not not_9 (not_9_out, in_27);
  and and_10 (and_10_out, in_28, in_10);
  or or_10 (or_10_out, in_28, in_10);
  xor xor_18 (xor_18_out, in_28, in_10);
  not not_10 (not_10_out, in_28);
  and and_11 (and_11_out, in_11, undriven);
  buf or_11 (or_11_out, in_11);  // OR_Gate
  xor xor_19 (xor_19_out, in_11, undriven);
  not not_11 (not_11_out, in_11);
  and and_12 (and_12_out, in_30, in_12);
  or or_12 (or_12_out, in_30, in_12);
  xor xor_20 (xor_20_out, in_30, in_12);
  not not_12 (not_12_out, in_30);
  and and_13 (and_13_out, in_31, in_13);
  or or_13 (or_13_out, in_31, in_13);
  xor xor_21 (xor_21_out, in_31, in_13);
  not not_13 (not_13_out, in_31);
  and and_14 (and_14_out, in_32, in_14);
  or or_14 (or_14_out, in_32, in_14);
  xor xor_22 (xor_22_out, in_32, in_14);
  not not_14 (not_14_out, in_32);
  and and_15 (and_15_out, A15, in_15);
  or or_15 (or_15_out, A15, in_15);
  xor xor_23 (xor_23_out, A15, in_15);
  not not_15 (not_15_out, A15);
  and and_16 (and_16_out, in_34, in_16);
  or or_16 (or_16_out, in_34, in_16);
  xor xor_24 (xor_24_out, in_34, in_16);
  not not_16 (not_16_out, in_34);
  Adder #(.width(1)) adder_9 (.a(in_27), .b(xor_25_out), .out(adder_9_out), .cin(adder_8_cout), .cout(adder_9_cout));
  xor xor_25 (xor_25_out, in_9, in_17);
  Adder #(.width(1)) adder_10 (.a(in_28), .b(xor_26_out), .out(adder_10_out), .cin(adder_9_cout), .cout(adder_10_cout));
  xor xor_26 (xor_26_out, in_10, in_17);
  Adder #(.width(1)) adder_11 (
    .a(in_11), .b(xor_27_out), .out(adder_11_out), .cin(adder_10_cout), .cout(adder_11_cout));
  xor xor_27 (xor_27_out, in_11, in_17);
  Adder #(.width(1)) adder_12 (
    .a(in_30), .b(xor_28_out), .out(adder_12_out), .cin(adder_11_cout), .cout(adder_12_cout));
  xor xor_28 (xor_28_out, in_12, in_17);
  Adder #(.width(1)) adder_13 (
    .a(in_31), .b(xor_29_out), .out(adder_13_out), .cin(adder_12_cout), .cout(adder_13_cout));
  xor xor_29 (xor_29_out, in_13, in_17);
  Adder #(.width(1)) adder_14 (
    .a(in_32), .b(xor_30_out), .out(adder_14_out), .cin(adder_13_cout), .cout(adder_14_cout));
  xor xor_30 (xor_30_out, in_14, in_17);
  Adder #(.width(1)) adder_15 (.a(A15), .b(xor_31_out), .out(adder_15_out), .cin(adder_14_cout), .cout(adder_15_cout));
  xor xor_31 (xor_31_out, in_15, in_17);
  Adder #(.width(1)) adder_16 (
    .a(in_34), .b(xor_32_out), .out(adder_16_out), .cin(adder_15_cout), .cout(adder_16_cout));
  xor xor_32 (xor_32_out, in_16, in_17);
  Multiplexer #(.select(2)) multiplexer_9 (
    .in0(and_9_out), .in1(or_9_out), .in2(xor_17_out), .in3(not_9_out), .out(multiplexer_9_out), .sel(S2));
  Multiplexer #(.select(2)) multiplexer_10 (
    .in0(and_10_out), .in1(or_10_out), .in2(xor_18_out), .in3(not_10_out), .out(multiplexer_10_out), .sel(S2));
  Multiplexer #(.select(2)) multiplexer_11 (
    .in0(and_11_out), .in1(or_11_out), .in2(xor_19_out), .in3(not_11_out), .out(multiplexer_11_out), .sel(S2));
  Multiplexer #(.select(2)) multiplexer_12 (
    .in0(and_12_out), .in1(or_12_out), .in2(xor_20_out), .in3(not_12_out), .out(multiplexer_12_out), .sel(S2));
  Multiplexer #(.select(2)) multiplexer_13 (
    .in0(and_13_out), .in1(or_13_out), .in2(xor_21_out), .in3(not_13_out), .out(multiplexer_13_out), .sel(S2));
  Multiplexer #(.select(2)) multiplexer_14 (
    .in0(and_14_out), .in1(or_14_out), .in2(xor_22_out), .in3(not_14_out), .out(multiplexer_14_out), .sel(S2));
  Multiplexer #(.select(2)) multiplexer_15 (
    .in0(and_15_out), .in1(or_15_out), .in2(xor_23_out), .in3(not_15_out), .out(multiplexer_15_out), .sel(S2));
  Multiplexer #(.select(2)) multiplexer_16 (
    .in0(and_16_out), .in1(or_16_out), .in2(xor_24_out), .in3(not_16_out), .out(multiplexer_16_out), .sel(S2));
  Multiplexer multiplexer_17 (.in0(adder_16_out), .in1(multiplexer_1_out), .out(multiplexer_17_out), .sel(in_36));
  Multiplexer multiplexer_18 (.in0(adder_15_out), .in1(multiplexer_2_out), .out(multiplexer_18_out), .sel(in_36));
  Multiplexer multiplexer_19 (.in0(adder_14_out), .in1(multiplexer_3_out), .out(multiplexer_19_out), .sel(in_36));
  Multiplexer multiplexer_20 (.in0(adder_13_out), .in1(multiplexer_4_out), .out(multiplexer_20_out), .sel(in_36));
  Multiplexer multiplexer_21 (.in0(adder_12_out), .in1(multiplexer_5_out), .out(multiplexer_21_out), .sel(in_36));
  Multiplexer multiplexer_22 (.in0(adder_11_out), .in1(multiplexer_6_out), .out(multiplexer_22_out), .sel(in_36));
  Multiplexer multiplexer_23 (.in0(adder_10_out), .in1(multiplexer_7_out), .out(multiplexer_23_out), .sel(in_36));
  Multiplexer multiplexer_24 (.in0(adder_9_out), .in1(multiplexer_8_out), .out(multiplexer_24_out), .sel(in_36));
  Multiplexer multiplexer_25 (.in0(adder_8_out), .in1(multiplexer_9_out), .out(multiplexer_25_out), .sel(in_36));
  Multiplexer multiplexer_26 (.in0(adder_7_out), .in1(multiplexer_10_out), .out(multiplexer_26_out), .sel(in_36));
  Multiplexer multiplexer_27 (.in0(adder_6_out), .in1(multiplexer_11_out), .out(multiplexer_27_out), .sel(in_36));
  Multiplexer multiplexer_28 (.in0(adder_5_out), .in1(multiplexer_12_out), .out(multiplexer_28_out), .sel(in_36));
  Multiplexer multiplexer_29 (.in0(adder_4_out), .in1(multiplexer_13_out), .out(multiplexer_29_out), .sel(in_36));
  Multiplexer multiplexer_30 (.in0(adder_3_out), .in1(multiplexer_14_out), .out(multiplexer_30_out), .sel(in_36));
  Multiplexer multiplexer_31 (.in0(adder_2_out), .in1(multiplexer_15_out), .out(multiplexer_31_out), .sel(in_36));
  Multiplexer multiplexer_32 (.in0(adder_1_out), .in1(multiplexer_16_out), .out(multiplexer_32_out), .sel(in_36));
  LED led_1 (.in(adder_16_cout));
  LED led_2 (.in(multiplexer_17_out));
  LED led_3 (.in(multiplexer_18_out));
  LED led_4 (.in(multiplexer_19_out));
  LED led_5 (.in(multiplexer_20_out));
  LED led_6 (.in(multiplexer_21_out));
  LED led_7 (.in(multiplexer_22_out));
  LED led_8 (.in(multiplexer_23_out));
  LED led_9 (.in(multiplexer_24_out));
  LED led_10 (.in(multiplexer_25_out));
  LED led_11 (.in(multiplexer_26_out));
  LED led_12 (.in(multiplexer_27_out));
  LED led_13 (.in(multiplexer_28_out));
  LED led_14 (.in(multiplexer_29_out));
  LED led_15 (.in(multiplexer_30_out));
  LED led_16 (.in(multiplexer_31_out));
  LED led_17 (.in(multiplexer_32_out));

  assign in_29 = in_11;

  // Notes on the sheet:
  //   A0
  //   S0,S1
  //   B0
  //   B15
  //   MODE A/S
  //   CIN
  //   CARRY OUT
  //   Y0
  //   Y15
endmodule
